# Fritzing sketch Geiger-PCB-V1 (saved by Fritzing 0.9.3b)
circuit board: 7cm x 5cm
breadboards: 1

parts:
  R2 = Resistor [tolerance=±5% resistance=4.7M package=THT]
  R3 = Resistor [tolerance=±5% resistance=100k package=THT]
  R4 = Resistor [tolerance=±5% resistance=10k package=THT]
  D1 = Rectifier Diode [part_number=1N4007 package="300 mil [THT]"]
  L1 = Inductor [part_number=15mH package="400 mil [THT]"]
  C1 = Ceramic Capacitor [capacitance=4.7nF package="100 mil [THT, multilayer]"]
  LED1 = RGB LED (com. cathode, rgb) [package="5 mm [THT]"]
  Q1 = NPN-Transistor [part_number=MPSA44 package="TO92 [THT]"]
  Q2 = NPN-Transistor [part_number=2N3904 package="TO92 [THT]"]
  R5 = Resistor [tolerance=±5% resistance=220 package=THT]
  R6 = Resistor [tolerance=±5% resistance=220 package=THT]
  R7 = Resistor [tolerance=±5% resistance=220 package=THT]
  Buzzer_Piezo = Piezo Speaker
  + = Screw terminal - 2 pins [package=THT]
  Arduino_NANO = Arduino Nano (Rev3.0)
  R1 = Resistor [tolerance=±5% resistance=220 package=THT]
  J2 = female pin header, 4 pins [form="♀ (female)"]
  J3 = female pin header, 1 pin [form="♀ (female)"]
  J4 = Screw terminal - 2 pins [package=THT]

nets:
  N1: R2.Pin_0, D1.cathode, C1.1
  N2: R2.Pin_1, +.pin2
  N3: R3.Pin_0, Q2.B, +.pin1
  N4: R3.Pin_1, C1.0, LED1.common_cathode, Q1.E, Q2.E, Buzzer_Piezo.pin2, Arduino_NANO.GND, J2.pin2, J4.pin1
  N5: R4.Pin_0, L1.pin_0, Arduino_NANO.5V, J2.pin1
  N6: R4.Pin_1, Q2.C, Arduino_NANO.D2
  N7: D1.anode, L1.pin_1, Q1.C
  N8: LED1.red_anode, R5.Pin_1
  N9: LED1.green_anode, R6.Pin_1
  N10: LED1.blue_anode, R7.Pin_1
  N11: Q1.B, R1.Pin_1
  N12: R5.Pin_0, Arduino_NANO.D8
  N13: R6.Pin_0, Arduino_NANO.D7
  N14: R7.Pin_0, Arduino_NANO.D6
  N15: Buzzer_Piezo.pin1, Arduino_NANO.D9, J3.pin1
  N16: Arduino_NANO.D5, R1.Pin_0
  N17: Arduino_NANO.VIN, J4.pin2
  N18: Arduino_NANO.A5, J2.pin4
  N19: Arduino_NANO.A4, J2.pin3

notes:
  GM Tube
  Geiger V1.0
  +
  -
  GM
  ->

// code stored in the sketch: geiger.ino
#include <Wire.h>    // Required for I2C communication
#include <LCD.h>
#include <LiquidCrystal_I2C.h>

#define I2C_ADDR    0x3F // <<----- Add your address here.  Find it from I2C Scanner
#define BACKLIGHT_PIN     3
#define En_pin  2
#define Rw_pin  1
#define Rs_pin  0
#define D4_pin  4
#define D5_pin  5
#define D6_pin  6
#define D7_pin  7
LiquidCrystal_I2C	lcd(I2C_ADDR, En_pin, Rw_pin, Rs_pin, D4_pin, D5_pin, D6_pin, D7_pin);

long count = 0;
long cpm = 0;
int led = 13;
double usv = 0.0;
int moyen[60];
int moyTemp =  0;
int tmp = 0;
long totalCount = 0;

int vert  = 7;
int rouge = 4;
int bleu  = 9;
int buzz  = 12;
void setup()  
{ 
	Serial.begin(9600);
	Serial.println("Booting...");
	Serial.println(" ");
	Serial.println("=================================");
	Serial.println("= Geiger-Muler Radiation Metter =");
	Serial.println("=================================");

	pinMode(led, OUTPUT);
	pinMode(vert, OUTPUT);
	pinMode(rouge, OUTPUT);
	pinMode(bleu, OUTPUT);
	pinMode(buzz, OUTPUT);
		
	Serial.println("Starting : i2c");
	Wire.begin();
	Serial.println("Starting : LCD");
	lcd.begin (16, 2); //  <<----- My LCD was 20x4
	lcd.setBacklightPin(BACKLIGHT_PIN, POSITIVE);
	lcd.setBacklight(HIGH);
	
	lcd.home();
  
  //uncomment this if runing on arduino 16mhz (uno, etc) 
  setPwmFrequency(5,64); 
  
  //setPwmFrequency(9,8); //pin 9 for 8Mhz. Comment this line if running on 16Mhz
  analogWrite(5, 180);   //starts PWM on pin 9. (replace 9 with 5 if runing on 16Mhz) 
  
  //calls 'countPulse' function when interupt pin goes low 
  //interupt 0 is pin 2 on the Arduino
  attachInterrupt(0,countPulse,FALLING); 
  
  for(int i=0; i<60; i++) moyen[i] = 0;
  
} 

void loop()  
{ 
	if(totalCount > 0) digitalWrite(led, 1);
  	
  delay(1000); //the count is incrementing during this delay
  
  //cpm = 6 *count; 
  usv = cpm * 0.0057;
  totalCount = totalCount + count;
	if(usv > 0.0) 
	{
		digitalWrite(rouge, 1);
		digitalWrite(vert, 0);
	}
	else
	{
		digitalWrite(rouge, 0);
		digitalWrite(vert, 1);
	}

  for(int i=0; i<60; i++) 
  {
  	tmp = i + 1;
  	moyen[i] = moyen[tmp];
  }
  
  moyen[60] = count;
  cpm = 0;
  for(int i=0; i<60; i++) cpm = cpm + moyen[i];
  
  Serial.print("Count = ");
  Serial.print(count);
  Serial.print(" / ");
  Serial.print("CPM = ");
  Serial.print(cpm,DEC);
  Serial.print(" / ");
  Serial.print("uSv = ");
  Serial.print(usv);
  Serial.print(" / ");
  Serial.print("TotalCount = ");
  Serial.println(totalCount);

	lcd.setCursor(0, 0);
	lcd.print("[        CPM   ]");
	lcd.setCursor(0, 1);
	lcd.print("[        uSv   ]");
  	lcd.setCursor(2, 0);
  	lcd.print(cpm); 
  	lcd.setCursor(2, 1);
  	lcd.print(usv); 
  
  count=0; //reset the count
  

                            
}


void setPwmFrequency(int pin, int divisor) {
  byte mode;
  if(pin == 5 || pin == 6 || pin == 9 || pin == 10) {
    switch(divisor) {
      case 1: mode = 0x01; break;
      case 8: mode = 0x02; break;
      case 64: mode = 0x03; break;
      case 256: mode = 0x04; break;
      case 1024: mode = 0x05; break;
      default: return;
    }
    if(pin == 5 || pin == 6) {
      TCCR0B = TCCR0B & 0b11111000 | mode;
    } else {
      TCCR1B = TCCR1B & 0b11111000 | mode;
    }
  } else if(pin == 3 || pin == 11) {
    switch(divisor) {
      case 1: mode = 0x01; break;
      case 8: mode = 0x02; break;
      case 32: mode = 0x03; break;
      case 64: mode = 0x04; break;
      case 128: mode = 0x05; break;
      case 256: mode = 0x06; break;
      case 1024: mode = 0x7; break;
      default: return;
    }
    TCCR2B = TCCR2B & 0b11111000 | mode;
  }
}

void countPulse(){
  digitalWrite(bleu, 1);
  digitalWrite(buzz, 1);
  detachInterrupt(0);
  count++; 
  while(digitalRead(2)==0){
  }
  attachInterrupt(0,countPulse,FALLING);
  digitalWrite(bleu, 0);
  digitalWrite(buzz, 0);

}
